# Fritzing sketch schematic (saved by Fritzing 0.9.3b)
circuit board: 6.88467cm x 5.3299cm

parts:
  Part1 = Arduino Leonardo (Rev3b)
  ATTINY-85 = attiny85 [package=dip]
  C1_10uF = Electrolytic Capacitor [capacitance=1µF package="100 mil [THT, electrolytic]"]
  JP3 = Header 2 [package=molex-1x2_lock]
  JP4 = Header 2 [package=molex-1x2_lock]
  JP5 = Header 2 [package=molex-1x2_lock]  # not connected
  JP6 = Header 2 [package=molex-1x2_lock]  # not connected

nets:
  N1: Part1.RESET, C1_10uF.+
  N2: Part1.5V, ATTINY-85.Pin_8
  N3: Part1.GND, ATTINY-85.Pin_4, C1_10uF.-, JP4.2
  N4: Part1.D10_PWM/A10, ATTINY-85.Pin_1
  N5: Part1.D11_PWM, ATTINY-85.Pin_5
  N6: Part1.D12/A11, ATTINY-85.Pin_6
  N7: Part1.D13_PWM, ATTINY-85.Pin_7
  N8: ATTINY-85.Pin_2, JP3.2
  N9: ATTINY-85.Pin_3, JP4.1

notes:
  CYBRnode (Solder)
  CYBRnode
  RST
  5V
  GND
  P0|PWM
  P1|PWM
  P2|A1
  P4|A2
  P#|A3
  ATTiny85 prototyping board
